# Fritzing sketch robot1 (saved by Fritzing 0.9.3b)
breadboards: 1

parts:
  Teensy_3_1 = Teensy 3.1
  HC-SR04_Sensor_1 = HC-SR04 Ultrasonic Distance Sensor
  HC-SR04_Sensor_2 = HC-SR04 Ultrasonic Distance Sensor
  HC-SR04_Sensor_3 = HC-SR04 Ultrasonic Distance Sensor
  Part1 = Adafruit VL53L0X Time of Flight Distance Sensor [part_number="Adafruit #3317"]
  Teensy_3_2 = Teensy 3.1
  Part2 = Bluetooth HC-05 Macho
  SERVO1 = Tower Pro SG90 servo [part_number=101246]
  SERVO2 = Tower Pro SG90 servo [part_number=101246]
  SERVO3 = Tower Pro SG90 servo [part_number=101246]

nets:
  GND: Teensy_3_1.GND, HC-SR04_Sensor_1.GND, HC-SR04_Sensor_2.GND, HC-SR04_Sensor_3.GND, Part1.GND, Teensy_3_2.GND, Part2.GND, SERVO1.GND, SERVO2.GND, SERVO3.GND
  N1: Teensy_3_1.D0, Part2.TXD
  N2: Teensy_3_1.D1, Part2.RXD
  N3: Teensy_3_1.D3, HC-SR04_Sensor_1.TRIG
  N4: Teensy_3_1.D4, HC-SR04_Sensor_1.ECHO
  N5: Teensy_3_1.D5, HC-SR04_Sensor_2.TRIG
  N6: Teensy_3_1.D6, HC-SR04_Sensor_2.ECHO
  N7: Teensy_3_1.D7, HC-SR04_Sensor_3.TRIG
  N8: Teensy_3_1.D8, HC-SR04_Sensor_3.ECHO
  N9: Teensy_3_1.D9, Teensy_3_2.D10
  N10: Teensy_3_1.D10, Teensy_3_2.D9
  N11: Teensy_3_1.A1/D15, SERVO3.Signal
  N12: Teensy_3_1.A4/D18, Part1.SDA
  N13: Teensy_3_1.A5/D19, Part1.XSHUT, Part1.SCL
  VCC: Teensy_3_1.Vin, HC-SR04_Sensor_1.VCC, HC-SR04_Sensor_2.VCC, HC-SR04_Sensor_3.VCC, Part1.VIN, Teensy_3_2.Vin, Part2.VCC, SERVO1.+5V, SERVO2.+5V, SERVO3.+5V
  N14: Teensy_3_2.A1/D15, SERVO2.Signal
  N15: Teensy_3_2.A2/D16, SERVO1.Signal

custom parts:
  Adafruit VL53L0X Time of Flight Distance Sensor: The VL53L0X is a Time of Flight distance sensor like no other you've used! The sensor contains a very tiny invisible laser source, and a matching sensor. The VL53L0X can detect the "time of flight", or how long the light has taken to bounce back to the sensor. Since it uses a very narrow light source, it is good for determining distance of only the surface directly in front of it. Unlike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
  Tower Pro SG90 servo: Original file by John De Cristofaro http://www.adafruit.com/products/1449 Adafruit Feedback Servo (Small) Edited by: e-radionica.com 28/9/2015
